// Logisim project proj_2_1.circ as structural Verilog: 9 circuits, main circuit testbench
module inst_fetch (
  input  clk,
  input  rst,
  input  control_en_i,
  input  [31:0] control_pc_i,
  input  [15:0] inst_i,
  output inst_en_o,
  output [31:0] current_pc_o,
  output [31:0] inst_addr_o,
  output [15:0] inst_o
);

  wire not_1_out, not_2_out;
  wire [31:0] adder_1_out, counter_1_q, multiplexer_1_out;

  not not_1 (not_1_out, rst);
  Adder #(.width(32)) adder_1 (.a(control_pc_i), .b(32'h1), .out(adder_1_out));  // open: cin, cout
  Counter #(.max('hffffffff), .width(32)) counter_1 (
    .clr(rst), .load(control_en_i), .up(not_1_out), .count(not_1_out), .clk(clk), .D(adder_1_out),
    .Q(counter_1_q));  // open: carry
  Multiplexer #(.width(32)) multiplexer_1 (
    .in0(counter_1_q), .in1(control_pc_i), .out(multiplexer_1_out), .sel(control_en_i));
  not not_2 (not_2_out, rst);
  Register #(.width(32)) register_1 (.D(multiplexer_1_out), .en(not_2_out), .clk(clk), .Q(current_pc_o), .clr(rst));
  not not_3 (inst_en_o, rst);

  assign inst_addr_o = current_pc_o;
  assign inst_o = inst_i;

  // Notes on the sheet:
  //   Don't touch
endmodule

module TOP (
  input  rst,
  input  clk,
  input  [15:0] inst,
  input  [31:0] mem_result,
  input  [31:0] current_pc,
  output mem_wen,
  output [31:0] mem_din,
  output mem_ren,
  output [31:0] alu_result,
  output control_en,
  output [31:0] control_pc,
  output wb_en,
  output [4:0] wb_addr,
  output [31:0] wb_data
);

  wire decoder_1_out0, decoder_1_out2, decoder_1_out8, decoder_1_out9, decoder_1_out10, decoder_1_out11,
       decoder_1_out12, decoder_1_out13, decoder_1_out14, decoder_1_out15, undriven;
  wire [4:0] addi_1_rd, bit_extender_1_out, li_1_rd, lui_1_rd, multiplexer_4_out, mv_1_rd, rd, rs2;
  wire [31:0] adder_1_out, adder_2_out, adder_3_out, imm, li_1_wb_data, lui_1_wb_data, multiplexer_3_out,
       multiplexer_5_out, multiplexer_6_out, multiplexer_7_out, register_2_q, register_3_q, register_4_q,
       register_5_q, register_6_q, register_7_q, register_8_q, register_9_q, register_10_q, register_11_q,
       shifter_1_out;

  Multiplexer #(.select(5), .width(32)) multiplexer_1 (
    .in9(li_1_wb_data), .in13(lui_1_wb_data), .in18(multiplexer_3_out), .out(alu_result),
    .sel({inst[15:13], inst[1:0]}));  // open: in0, in1, in2, in3, in4, in5, in6, in7, in8, in10, in11, in12, in14, in15, in16, in17, in19, in20, in21, in22, in23, in24, in25, in26, in27, in28, in29, in30, in31
  Multiplexer #(.select(5), .width(5)) multiplexer_2 (
    .in1(addi_1_rd), .in9(li_1_rd), .in13(lui_1_rd), .in16(rd), .in18(multiplexer_4_out), .out(wb_addr),
    .sel({inst[15:13], inst[1:0]}));  // open: in0, in2, in3, in4, in5, in6, in7, in8, in10, in11, in12, in14, in15, in17, in19, in20, in21, in22, in23, in24, in25, in26, in27, in28, in29, in30, in31
  Decoder #(.select(5)) decoder_1 (
    .out0(decoder_1_out0), .out2(decoder_1_out2), .out8(decoder_1_out8), .out9(decoder_1_out9),
    .out10(decoder_1_out10), .out11(decoder_1_out11), .out12(decoder_1_out12), .out13(decoder_1_out13),
    .out14(decoder_1_out14), .out15(decoder_1_out15), .sel(wb_addr), .en(undriven));  // open: out1, out3, out4, out5, out6, out7, out16, out17, out18, out19, out20, out21, out22, out23, out24, out25, out26, out27, out28, out29, out30, out31
  Adder #(.width(32)) adder_1 (.a(current_pc), .b(32'h1), .out(adder_1_out));  // open: cin, cout
  Register #(.width(32)) register_1 (.D(adder_1_out), .en(1'b1), .clk(clk), .Q(control_pc));  // open: clr
  Multiplexer #(.width(32)) multiplexer_3 (.out(multiplexer_3_out), .sel(inst[2]));  // open: in0, in1
  Multiplexer #(.width(5)) multiplexer_4 (.in0(mv_1_rd), .in1(rd), .out(multiplexer_4_out), .sel(inst[2]));
  Register #(.width(32)) register_2 (.D(alu_result), .en(decoder_1_out0), .clk(clk), .Q(register_2_q));  // open: clr
  Register #(.width(32)) register_3 (.D(alu_result), .en(decoder_1_out2), .clk(clk), .Q(register_3_q));  // open: clr
  Register #(.width(32)) register_4 (.D(alu_result), .en(decoder_1_out8), .clk(clk), .Q(register_4_q));  // open: clr
  Register #(.width(32)) register_5 (.D(alu_result), .en(decoder_1_out9), .clk(clk), .Q(register_5_q));  // open: clr
  Register #(.width(32)) register_6 (.D(alu_result), .en(decoder_1_out10), .clk(clk), .Q(register_6_q));  // open: clr
  Register #(.width(32)) register_7 (.D(alu_result), .en(decoder_1_out11), .clk(clk), .Q(register_7_q));  // open: clr
  li li_1 (.inst(inst), .rd(li_1_rd), .wb_data(li_1_wb_data));
  lui lui_1 (.inst(inst), .rd(lui_1_rd), .wb_data(lui_1_wb_data));
  add add_1 (.inst(inst), .ts2(rs2), .rd(rd));
  addi addi_1 (.inst(inst), .rd(addi_1_rd), .imm(imm));
  Register #(.width(32)) register_8 (.D(alu_result), .en(decoder_1_out12), .clk(clk), .Q(register_8_q));  // open: clr
  Register #(.width(32)) register_9 (.D(alu_result), .en(decoder_1_out13), .clk(clk), .Q(register_9_q));  // open: clr
  Register #(.width(32)) register_10 (.D(alu_result), .en(decoder_1_out14), .clk(clk), .Q(register_10_q));  // open: clr
  Register #(.width(32)) register_11 (.D(alu_result), .en(decoder_1_out15), .clk(clk), .Q(register_11_q));  // open: clr
  slli slli_1 (.inst(inst), .rd(rd), .imm(imm));
  mv mv_1 (.inst(inst), .ts2(rs2), .rd(mv_1_rd));
  Multiplexer #(.select(5), .width(32)) multiplexer_5 (
    .in0(register_2_q), .in2(register_3_q), .in8(register_4_q), .in9(register_5_q), .in10(register_6_q),
    .in11(register_7_q), .in12(register_8_q), .in13(register_9_q), .in14(register_10_q),
    .in15(register_11_q), .out(multiplexer_5_out), .sel(rd));  // open: in1, in3, in4, in5, in6, in7, in16, in17, in18, in19, in20, in21, in22, in23, in24, in25, in26, in27, in28, in29, in30, in31
  Multiplexer #(.select(5), .width(32)) multiplexer_6 (
    .in0(register_2_q), .in2(register_3_q), .in8(register_4_q), .in9(register_5_q), .in10(register_6_q),
    .in11(register_7_q), .in12(register_8_q), .in13(register_9_q), .in14(register_10_q),
    .in15(register_11_q), .out(multiplexer_6_out), .sel(rs2));  // open: in1, in3, in4, in5, in6, in7, in16, in17, in18, in19, in20, in21, in22, in23, in24, in25, in26, in27, in28, in29, in30, in31
  Bit_Extender #(.in_width(32), .out_width(5)) bit_extender_1 (.in(imm), .out(bit_extender_1_out));
  Adder #(.width(32)) adder_2 (.a(multiplexer_5_out), .b(multiplexer_6_out), .out(adder_2_out));  // open: cin, cout
  Adder #(.width(32)) adder_3 (.a(multiplexer_5_out), .b(imm), .out(adder_3_out));  // open: cin, cout
  Shifter #(.width(32)) shifter_1 (.in(multiplexer_5_out), .\dist (bit_extender_1_out), .out(shifter_1_out));
  Multiplexer #(.width(32)) multiplexer_7 (
    .in0(multiplexer_6_out), .in1(adder_2_out), .out(multiplexer_7_out), .sel(inst[2]));
  Multiplexer #(.select(5), .width(32)) multiplexer_8 (
    .in1(adder_3_out), .in16(shifter_1_out), .in18(multiplexer_7_out), .out(alu_result),
    .sel({inst[15:13], inst[1:0]}));  // open: in0, in2, in3, in4, in5, in6, in7, in8, in9, in10, in11, in12, in13, in14, in15, in17, in19, in20, in21, in22, in23, in24, in25, in26, in27, in28, in29, in30, in31

  assign control_en = 1'b0;
  assign mem_din = {32{1'b0}};
  assign mem_ren = 1'b0;
  assign mem_wen = 1'b0;
  assign wb_data = alu_result;
  assign wb_en = 1'b1;

  // Other names for the same wires on the sheet: func4 = inst[2]

  // Notes on the sheet:
  //   Fixed I/O
  //   Don't touch
endmodule

module testbench (
  input  rst,
  output mem_wen,
  output [31:0] mem_din,
  output mem_ren,
  output [31:0] alu_result,
  output control_en,
  output [31:0] control_pc,
  output halt,
  output wb_en,
  output [4:0] wb_addr,
  output [31:0] wb_data
);

  wire clk, inst_en, not_1_out, not_2_out, not_3_out, not_4_out, por_1_out, rst_t;
  wire [15:0] inst, inst_i;
  wire [31:0] current_pc, inst_addr, mem_result;

  not not_1 (not_1_out, inst_i[0]);
  not not_2 (not_2_out, inst_i[1]);
  not not_3 (not_3_out, inst_i[13]);
  not not_4 (not_4_out, inst_i[14]);
  and and_1 (halt, not_1_out, not_2_out, not_3_out, not_4_out, inst_i[15]);
  Clock clock_1 (.out(clk));
  or or_1 (rst_t, rst, por_1_out);
  POR por_1 (.out(por_1_out));
  inst_fetch inst_fetch_1 (
    .clk(clk), .rst(rst_t), .control_en_i(control_en), .control_pc_i(control_pc), .inst_i(inst_i),
    .inst_en_o(inst_en), .current_pc_o(current_pc), .inst_addr_o(inst_addr), .inst_o(inst));
  TOP top_1 (
    .rst(rst_t), .clk(clk), .inst(inst), .mem_result(mem_result), .current_pc(current_pc), .mem_wen(mem_wen),
    .mem_din(mem_din), .mem_ren(mem_ren), .alu_result(alu_result), .control_en(control_en),
    .control_pc(control_pc), .wb_en(wb_en), .wb_addr(wb_addr), .wb_data(wb_data));
  ROM #(.dataWidth(16)) rom_1 (.addr(inst_addr[7:0]), .data(inst_i));
  RAM #(.addrWidth(16), .clearpin("true"), .dataWidth(32), .\type ("nonvolatile")) ram_1 (
    .addr(alu_result[15:0]), .we(mem_wen), .oe(mem_ren), .clk(clk), .din(mem_din), .dout(mem_result),
    .clr(rst_t));

  // Notes on the sheet:
  //   contents of rom_1 (hex, n*v repeats v):
  //   4425 6525 40e 942a 84a2 49d 8000 1 1
  //   you can write any instruction in
endmodule

module li (
  input  [15:0] inst,
  output [4:0] rd,
  output [31:0] wb_data
);

  assign wb_data = {{26{inst[12]}}, {inst[12], inst[6:2]}};  // Bit_Extender bit_extender_1

  assign rd = inst[11:7];

  // Other names for the same wires on the sheet: wb_addr[4:0] = inst[11:7]
endmodule

module lui (
  input  [15:0] inst,
  output [4:0] rd,
  output [31:0] wb_data
);

  wire [31:0] li_1_wb_data;

  li li_1 (.inst(inst), .rd(rd), .wb_data(li_1_wb_data));
  Shifter #(.width(32)) shifter_1 (.in(li_1_wb_data), .\dist (5'b01100), .out(wb_data));
endmodule

module add (
  input  [15:0] inst,
  output [4:0] ts2,
  output [4:0] rd
);


  assign rd = inst[11:7];
  assign ts2 = inst[6:2];

  // Other names for the same wires on the sheet: rs2[4:0] = inst[6:2]
endmodule

module addi (
  input  [15:0] inst,
  output [4:0] rd,
  output [31:0] imm
);

  assign imm = {{26{inst[12]}}, {inst[12], inst[6:2]}};  // Bit_Extender bit_extender_1

  assign rd = inst[11:7];
endmodule

module mv (
  input  [15:0] inst,
  output [4:0] ts2,
  output [4:0] rd
);


  assign rd = inst[11:7];
  assign ts2 = inst[6:2];

  // Other names for the same wires on the sheet: rs2[4:0] = inst[6:2]
endmodule

module slli (
  input  [15:0] inst,
  output [4:0] rd,
  output [31:0] imm
);

  addi addi_1 (.inst(inst), .rd(rd), .imm(imm));
endmodule
